// Logisim project Lab2-Part1-2001-Hanling.circ as structural Verilog: 1 circuit, main circuit main
module main (
  input  W,
  input  X,
  input  Y
);

  wire and_1_out, and_2_out, and_3_out, or_1_out;

  and and_1 (and_1_out, ~W, X);  // AND_Gate
  and and_2 (and_2_out, W, ~X);  // AND_Gate
  or or_1 (or_1_out, and_1_out, and_2_out);
  and and_3 (and_3_out, or_1_out, Y);
  // Probe on and_3_out

  // Notes on the sheet:
  //   MIDN Mike Hanling 202430
  //   Logisim Lab Part 1
  //   y
endmodule
