// Logisim project Lab2-Part2-2001-Hanling.circ as structural Verilog: 1 circuit, main circuit main
module main (
  input  W,
  input  X,
  input  Y,
  input  Z
);

  wire and_1_out, and_2_out, and_3_out, and_4_out, and_5_out, and_6_out, nor_1_out, or_1_out, or_2_out;

  and and_1 (and_1_out, ~W, Y);  // AND_Gate
  and and_2 (and_2_out, W, ~Y);  // AND_Gate
  and and_3 (and_3_out, ~W, ~X, Z);  // AND_Gate
  and and_4 (and_4_out, W, X, ~Z);  // AND_Gate
  and and_5 (and_5_out, ~X, Y, Z);  // AND_Gate
  and and_6 (and_6_out, X, ~Y, ~Z);  // AND_Gate
  // Probe on or_1_out
  or or_1 (or_1_out, and_1_out, and_3_out, and_5_out);
  or or_2 (or_2_out, and_2_out, and_4_out, and_6_out);
  // Probe on or_2_out
  nor nor_1 (nor_1_out, or_1_out, or_2_out);
  // Probe on nor_1_out

  // Notes on the sheet:
  //   MIDN Mike Hanling 202430
  //   Logisim Lab Part 2
  //   LessThan
  //   GreaterThan
  //   EqualTo
endmodule
